# Fritzing sketch circuit (saved by Fritzing 0.9.0b)
stripboards: 1

parts:
  Part1 = Arduino Nano (Rev3.0)
  S1 = Pushbutton [package="[THT]"]
  C1 = Ceramic Capacitor [capacitance=100nF package="100 mil [THT, multilayer]"]
  R1 = Resistor [tolerance=±5% resistance=10k package=THT]
  LED1 = LED - 5mm [color="Red (633nm)" package="5 mm [THT]"]
  LED2 = LED - 5mm [color="Red (633nm)" package="5 mm [THT]"]
  R2 = Resistor [tolerance=±5% resistance=2.2k package=THT]
  R3 = Resistor [tolerance=±5% resistance=2.2k package=THT]
  IC1 = IC, DIP package, 16 pins [chip_label=IC part_number=SL486]
  C2 = Ceramic Capacitor [capacitance=0.1nF part_number=220pF package="100 mil [THT, multilayer]"]
  C3 = Electrolytic Capacitor [capacitance=22µF package="100 mil [THT, electrolytic]"]
  C4 = Ceramic Capacitor [capacitance=150nF package="100 mil [THT, multilayer]"]
  R4 = Resistor [tolerance=±5% resistance=51 package=THT]
  C5 = Electrolytic Capacitor [capacitance=10µF part_number=6.8uF package="100 mil [THT, electrolytic]"]
  C6 = Electrolytic Capacitor [capacitance=1µF part_number=68uF package="100 mil [THT, electrolytic]"]
  C7 = Electrolytic Capacitor [capacitance=10µF package="100 mil [THT, electrolytic]"]
  C8 = Ceramic Capacitor [capacitance=10nF part_number=4.7nF package="100 mil [THT, multilayer]"]
  C9 = Ceramic Capacitor [capacitance=10nF part_number=22nF package="100 mil [THT, multilayer]"]
  C10 = Ceramic Capacitor [capacitance=100nF part_number=22nF package="100 mil [THT, multilayer]"]
  Q1 = MOSFET-NCHANNEL [part_number=2n7000 package=to-92]
  P1 = S1133 Si Photodiode [part_number=BPW41N package="8mm Ceramic [THT]"]
  LED3 = LED - 5mm [color="Infrared (940nm)" package="5 mm [THT]"]
  R5 = Resistor [tolerance=±5% resistance=10 package=THT]
  R6 = Resistor [tolerance=±5% resistance=100 package=THT]
  R7 = Resistor [tolerance=±5% resistance=100k package=THT]
  Q2 = MOSFET-NCHANNEL [part_number=2n7000 package=to-92]
  LED4 = LED - 5mm [color="Infrared (940nm)" package="5 mm [THT]"]
  R9 = Resistor [tolerance=±5% resistance=100 package=THT]
  R10 = Resistor [tolerance=±5% resistance=100k package=THT]
  R11 = TRIMPOT [part_number=1k package=3386u]
  D12 = Diode [part_number=1n4448 package=diode-1n4001]
  D13 = Diode [part_number=1n4448 package=diode-1n4001]
  R12 = Resistor [tolerance=±5% resistance=220 package=THT]
  VCC1 = Battery block 9V
  J1 = female pin header, 4 pins [form="♀ (female)"]
  D17 = Diode [part_number=1n4448 package=diode-1n4001]
  D18 = Diode [part_number=1n4448 package=diode-1n4001]
  R13 = Resistor [tolerance=±5% resistance=220 package=THT]
  P2 = S1133 Si Photodiode [part_number=BPW41N package="8mm Ceramic [THT]"]
  U1 = LM 358 Dual Op-Amp [package="DIP8 [THT]"]
  LED5 = LED - 5mm [color="Red (633nm)" package="5 mm [THT]"]
  R14 = Resistor [tolerance=±5% resistance=100 package=THT]
  R15 = Resistor [tolerance=±5% resistance=10k package=THT]
  R16 = Resistor [tolerance=±5% resistance=10k package=THT]
  R18 = Resistor [tolerance=±10% resistance=680k package=THT]
  R19 = TRIMPOT [part_number=1k package=3386u]
  R20 = Resistor [tolerance=±10% resistance=680k package=THT]
  C11 = Ceramic Capacitor [capacitance=100nF package="100 mil [THT, multilayer]"]

nets:
  D2: Part1.D2, R12.Pin_1
  D3: Part1.D3, R13.Pin_1
  D4: Part1.D4, R14.Pin_0
  D5: Part1.D5, LED5.cathode
  D6: Part1.D6, R6.Pin_0
  D7: Part1.D7, R9.Pin_0
  D8: Part1.D8, IC1.pin11
  D9: Part1.D9
  D10: Part1.D10
  5V: Part1.5V, S1.Pin_3, S1.Pin_4, C1.1, IC1.pin7, C3.+, R4.Pin_0, C8.0, D12.C, D18.C, P2.anode, U1.connector7, R15.Pin_0, R19.CW
  A1: S1.Pin_1, S1.Pin_2, C1.0, R1.Pin_0
  GND: R1.Pin_1, LED1.cathode, LED2.cathode, IC1.pin12, IC1.pin13, IC1.pin14, C3.-, C4.0, C7.-, C10.1, Q1.S, R7.Pin_1, Q2.S, R10.Pin_1, D13.A, VCC1.-, J1.pin4, D17.A, U1.connector3, R16.Pin_1, R19.CCW, C11.0
  N1: LED1.anode, R2.Pin_1
  N2: LED2.anode, R3.Pin_1
  A2: R2.Pin_0
  A3: R3.Pin_0
  N3: IC1.pin1, P1.anode
  N4: IC1.pin2, C5.-
  N5: IC1.pin3, C6.-
  N6: IC1.pin4, R4.Pin_1, C5.+, C6.+, C7.+, C9.0
  N7: IC1.pin5, C9.1
  N8: IC1.pin6, C8.1
  N9: IC1.pin8, C4.1
  N10: IC1.pin9, C2.0
  N11: IC1.pin10, C2.1
  N12: IC1.pin15, C10.0
  N13: IC1.pin16, P1.cathode
  N14: Q1.D, R5.Pin_1
  N15: Q1.G, R6.Pin_1, R7.Pin_0
  N16: LED3.cathode, R5.Pin_0
  N17: Q2.G, R9.Pin_1, R10.Pin_0
  N18: LED4.cathode, R11.WIPER
  N19: D12.A, D13.C
  N20: R12.Pin_0, J1.pin2
  N21: VCC1.+, J1.pin1
  N22: J1.pin3, R13.Pin_0
  N23: D17.C, D18.A
  N24: P2.cathode, U1.connector1, R18.Pin_1
  N25: U1.connector0, R18.Pin_0, R20.Pin_1
  N26: U1.connector2, R19.WIPER
  N27: U1.connector4, R15.Pin_1, R16.Pin_0
  N28: U1.connector5, U1.connector6
  N29: LED5.anode, R14.Pin_1
  A0: R20.Pin_0

notes:
  IR Beacon Tester, RJ
  LED Detect
  Status LEDs
  To Reciever Under Test
  IR Reciever and Amp
  IR TX High Power
  IR TX Low Power
  Start Button
